# Fritzing sketch recieve (saved by Fritzing 0.9.3b)
breadboards: 1

parts:
  U1 = atmega328 [package=dip]
  Part1 = FTDI Basic Programmer
  Part2 = NRF24L01

nets:
  N1: U1.D0_(RX), Part1.TXO
  N2: U1.D1_(TX), Part1.RXI
  N3: U1.D2, Part2.IRQ
  5V: U1.VCC, Part1.POWER
  N4: U1.D9_(PWM), Part2.CE
  N5: U1.D10_(PWM), Part2.CSN
  N6: U1.D11_(PWM), Part2.MOSI
  N7: U1.D12, Part2.MISO
  N8: U1.D13, Part2.SCK
  3.3V: Part2.VCC
  GND: Part2.GND
